# Fritzing sketch demo_circuit (saved by Fritzing 0.9.6b)
breadboards: 1

parts:
  Part1 = Arduino Uno (Rev3)
  S1 = Pushbutton [package="[THT]"]
  R1 = Resistor [tolerance=±5% resistance=10 package=THT]  # not connected
  LED1 = LED - 5mm [color="Red (633nm)" package="5 mm [THT]"]  # not connected
  R2 = Resistor [tolerance=±5% resistance=150 package=THT]  # not connected
  LED2 = LED - 5mm [color="Green (565nm)" package="5 mm [THT]"]  # not connected
  R3 = Resistor [tolerance=±5% resistance=150 package=THT]  # not connected
  Mod1 = KY-016 RGB Full Color LED Module [package="Breakout board"]  # not connected
  J1 = Basic Servo

nets:
  N1: Part1.D6_PWM, J1.pulse
  5V: Part1.5V, J1.vcc
  GND: Part1.GND, J1.gnd
  N2: S1.Pin_1, S1.Pin_2
  N3: S1.Pin_3, S1.Pin_4

custom parts:
  KY-016 RGB Full Color LED Module: KY-016 Arduino full color 5mm RGB LED, different colors can be obtained by mixing the three primary colors.
